# Fritzing sketch lg_schematic (saved by Fritzing 0.9.5d)

parts:
  U1 = ESP32S-HiLetgo [part_number=ESP32S-HiLetgo]
  WS2812B1 = WS2812B 12V Strip -- White (60/m)
  WS2812B2 = WS2812B 12V Strip -- White (60/m)
  WS2812B3 = WS2812B 12V Strip -- White (60/m)
  WS2812B4 = WS2812B 12V Strip -- White (60/m)
  WS2812B7 = WS2812B 12V Strip -- White (60/m)
  WS2812B8 = WS2812B 12V Strip -- White (60/m)
  WS2812B10 = WS2812B 12V Strip -- White (60/m)
  WS2812B11 = WS2812B 12V Strip -- White (60/m)
  WS2812B12 = WS2812B 12V Strip -- White (60/m)
  J3 = Power Jack [package=power_jack_smd]
  D1 = Schottky Diode 800mil [package="800 mil [THT]"]

nets:
  N1: U1.GND, WS2812B1.+12V#1, J3.GNDBREAK
  N2: U1.GPIO18, WS2812B1.DI
  N3: U1.IN, D1.cathode
  N4: WS2812B1.GND#3, J3.GND, D1.anode
  N5: WS2812B1.GND#4, WS2812B2.GND#3
  N6: WS2812B1.DO, WS2812B2.DI
  N7: WS2812B1.+12V#6, WS2812B2.+12V#1
  N8: WS2812B2.GND#4, WS2812B4.GND#3
  N9: WS2812B2.DO, WS2812B4.DI
  N10: WS2812B2.+12V#6, WS2812B4.+12V#1
  N11: WS2812B3.+12V#1, WS2812B4.+12V#6
  N12: WS2812B3.DI, WS2812B4.DO
  N13: WS2812B3.GND#3, WS2812B4.GND#4
  N14: WS2812B3.GND#4, WS2812B8.GND#3
  N15: WS2812B3.DO, WS2812B8.DI
  N16: WS2812B3.+12V#6, WS2812B8.+12V#1
  N17: WS2812B7.+12V#1, WS2812B8.+12V#6
  N18: WS2812B7.DI, WS2812B8.DO
  N19: WS2812B7.GND#3, WS2812B8.GND#4
  N20: WS2812B7.GND#4, WS2812B11.GND#3
  N21: WS2812B7.DO, WS2812B11.DI
  N22: WS2812B7.+12V#6, WS2812B11.+12V#1
  N23: WS2812B10.+12V, WS2812B12.+12V#6
  N24: WS2812B10.DI, WS2812B12.DO
  N25: WS2812B10.GND, WS2812B12.GND#4
  N26: WS2812B11.GND#4, WS2812B12.GND#3
  N27: WS2812B11.DO, WS2812B12.DI
  N28: WS2812B11.+12V#6, WS2812B12.+12V#1

custom parts:
  ESP32S-HiLetgo: HiLetgo ESP-WROOM-32 ESP32 ESP-32S Development Board 2.4GHz Dual-Mode WiFi + Bluetooth Dual Cores Microcontroller The ESP32 integrated with Antenna switches, RF Balun, power amplifiers, low-noise amplifiers, filters, and management modules, and the entire solution occupies the least area of PCB. 2.4 GHz Wi-Fi plus Bluetooth dual-mode chip, with TSMC Ultra-low power consumption 40nm technology,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
  WS2812B 12V Strip -- White (60/m): WS2812B LED Strip, White, 60 pixels per meter, 12V Power
  Schottky Diode 800mil: A standard schottky barrier rectifier diode - 800mil
